# Fritzing sketch box2 (saved by Fritzing 0.9.3b)
perfboards: 1

parts:
  J1 = screw terminal, 4 pins
  J2 = screw terminal, 4 pins
  J3 = female pin header, 4 pins [form="♀ (female)"]
  Part1 = BluePill

nets:
  N1: J1.pin1, J3.pin4, Part1.GND3
  N2: J1.pin4, J2.pin4, J3.pin1, Part1.5V
  N3: J2.pin1, Part1.B11
  N4: J2.pin2, Part1.B10
  N5: J2.pin3, Part1.GND
  N6: J3.pin2, Part1.B8
  N7: J3.pin3, Part1.B9
