# Fritzing sketch box3 (saved by Fritzing 0.9.3b)
perfboards: 1

parts:
  J1 = female pin header, 4 pins [form="♀ (female)"]
  J2 = screw terminal, 4 pins

nets:
  N1: J1.pin1, J2.pin1
  N2: J1.pin2, J2.pin2
  N3: J1.pin3, J2.pin3
  N4: J1.pin4, J2.pin4
